// Logisim project Parallel Adder.circ as structural Verilog: 1 circuit, main circuit main
module main (
  input  [3:0] in_1,
  input  in_2,
  input  [3:0] in_3,
  input  [3:0] in_4,
  output [3:0] out_5,
  output out_6
);

  wire button_1_out;
  wire [3:0] register_1_q, register_2_q, xor_1_out;

  Button button_1 (.out(button_1_out));
  Register #(.width(4)) register_1 (.D(in_1), .Q(register_1_q), .clk(button_1_out));  // open: en, clr
  Register #(.width(4)) register_2 (.D(in_3), .Q(register_2_q), .clk(button_1_out));  // open: en, clr
  assign xor_1_out = register_2_q ^ in_4;  // XOR_Gate xor_1, 4 bits wide
  Adder #(.width(4)) adder_1 (.a(register_1_q), .b(xor_1_out), .out(out_5), .cin(in_2), .cout(out_6));
endmodule
