// Logisim project cao.circ as structural Verilog: 1 circuit, main circuit main
module main (
  input  in_1,
  input  in_2,
  input  in_3,
  input  in_4,
  input  in_5,
  input  in_6,
  input  in_7,
  input  B3,
  input  B2,
  input  B1,
  input  B0,
  input  in_12,
  input  A3,
  input  [1:0] S3_S4,
  input  A2,
  input  A1,
  input  A0,
  input  in_18,
  input  [1:0] S1_S0,
  input  in_20,
  input  Cin,
  input  in_22,
  input  in_23,
  input  in_24,
  input  in_25,
  output out_26,
  output out_27,
  output out_28,
  output out_29,
  output out_30,
  output out_31,
  output out_32,
  output out_33,
  output out_34,
  output out_35,
  output out_36,
  output out_37,
  output out_38
);

  wire adder_1_cout, adder_1_out, adder_2_cout, adder_2_out, adder_3_cout, adder_3_out, adder_4_out,
       and_1_out, and_2_out, and_3_out, and_4_out, multiplexer_1_out, multiplexer_2_out, multiplexer_3_out,
       multiplexer_4_out, multiplexer_5_out, multiplexer_6_out, multiplexer_7_out, multiplexer_8_out,
       multiplexer_9_out, multiplexer_10_out, multiplexer_11_out, multiplexer_12_out, not_1_out, not_2_out,
       not_3_out, not_4_out, not_5_out, not_6_out, not_7_out, or_1_out, or_2_out, or_3_out, or_4_out,
       xor_1_out, xor_2_out, xor_3_out, xor_4_out;

  Multiplexer multiplexer_1 (.in0(in_1), .in1(A1), .out(multiplexer_1_out), .sel(in_3));  // open: en
  Multiplexer multiplexer_2 (.in0(B3), .in1(A2), .out(multiplexer_2_out), .sel(in_3));  // open: en
  Multiplexer multiplexer_3 (.in0(A1), .in1(A3), .out(multiplexer_3_out), .sel(in_3));  // open: en
  Multiplexer multiplexer_4 (.in0(A2), .in1(in_2), .out(multiplexer_4_out), .sel(in_3));  // open: en
  Multiplexer multiplexer_5 (.in0(in_4), .in1(A1), .out(multiplexer_5_out), .sel(in_6));  // open: en
  Multiplexer multiplexer_6 (.in0(B3), .in1(A2), .out(multiplexer_6_out), .sel(in_6));  // open: en
  Multiplexer multiplexer_7 (.in0(A1), .in1(A3), .out(multiplexer_7_out), .sel(in_6));  // open: en
  Multiplexer multiplexer_8 (.in0(A2), .in1(in_5), .out(multiplexer_8_out), .sel(in_6));  // open: en
  Multiplexer multiplexer_9 (.in0(B3), .in1(A3), .out(multiplexer_9_out), .sel(in_7));  // open: en
  xor xor_1 (xor_1_out, B3, A3);
  or or_1 (or_1_out, B3, A3);
  and and_1 (and_1_out, B3, A3);
  Multiplexer multiplexer_10 (.in0(B2), .in1(A2), .out(multiplexer_10_out), .sel(in_12));  // open: en
  xor xor_2 (xor_2_out, B2, A2);
  or or_2 (or_2_out, B2, A2);
  and and_2 (and_2_out, B2, A2);
  Multiplexer multiplexer_11 (.in0(B1), .in1(A1), .out(multiplexer_11_out), .sel(in_18));  // open: en
  xor xor_3 (xor_3_out, B1, A1);
  or or_3 (or_3_out, B1, A1);
  and and_3 (and_3_out, B1, A1);
  Multiplexer multiplexer_12 (.in0(B0), .in1(A1), .out(multiplexer_12_out), .sel(in_20));  // open: en
  xor xor_4 (xor_4_out, B0, A1);
  or or_4 (or_4_out, B0, A1);
  and and_4 (and_4_out, B0, A1);
  not not_1 (not_1_out, multiplexer_9_out);
  not not_2 (not_2_out, multiplexer_10_out);
  not not_3 (not_3_out, 1'b1);
  not not_4 (not_4_out, B0);
  not not_5 (not_5_out, B1);
  not not_6 (not_6_out, B2);
  not not_7 (not_7_out, B3);
  Multiplexer #(.select(2)) multiplexer_13 (
    .in0(1'b1), .in1(not_3_out), .in2(not_4_out), .in3(B0), .out(out_34), .sel(S1_S0), .en(in_22));
  Multiplexer #(.select(2)) multiplexer_14 (
    .in0(1'b1), .in1(not_3_out), .in2(not_5_out), .in3(B1), .out(out_35), .sel(S1_S0), .en(in_23));
  Multiplexer #(.select(2)) multiplexer_15 (
    .in0(1'b1), .in1(not_3_out), .in2(not_6_out), .in3(B2), .out(out_36), .sel(S1_S0), .en(in_24));
  Multiplexer #(.select(2)) multiplexer_16 (
    .in0(1'b1), .in1(not_3_out), .in2(not_7_out), .in3(B3), .out(out_37), .sel(S1_S0), .en(in_25));
  Multiplexer #(.select(2)) multiplexer_17 (
    .in0(not_1_out), .in1(xor_1_out), .in2(or_1_out), .in3(and_1_out), .out(out_26), .sel(S1_S0));  // open: en
  Multiplexer #(.select(2)) multiplexer_18 (
    .in0(not_2_out), .in1(xor_2_out), .in2(or_2_out), .in3(and_2_out), .out(out_27), .sel(S1_S0));  // open: en
  Multiplexer #(.select(2)) multiplexer_19 (
    .in0(multiplexer_11_out), .in1(xor_3_out), .in2(or_3_out), .in3(and_3_out), .out(out_30), .sel(S1_S0));  // open: en
  Multiplexer #(.select(2)) multiplexer_20 (
    .in0(multiplexer_12_out), .in1(xor_4_out), .in2(or_4_out), .in3(and_4_out), .out(out_33), .sel(S1_S0));  // open: en
  Adder #(.width(1)) adder_1 (.a(out_34), .b(A0), .out(adder_1_out), .cin(Cin), .cout(adder_1_cout));
  Adder #(.width(1)) adder_2 (.a(out_35), .b(A1), .out(adder_2_out), .cin(adder_1_cout), .cout(adder_2_cout));
  Adder #(.width(1)) adder_3 (.a(out_36), .b(A2), .out(adder_3_out), .cin(adder_2_cout), .cout(adder_3_cout));
  Adder #(.width(1)) adder_4 (.a(out_37), .b(A3), .out(adder_4_out), .cin(adder_3_cout), .cout(out_38));
  Multiplexer #(.select(2)) multiplexer_21 (
    .in0(multiplexer_1_out), .in1(multiplexer_5_out), .in2(out_26), .in3(adder_1_out), .out(out_28),
    .sel(S3_S4));  // open: en
  Multiplexer #(.select(2)) multiplexer_22 (
    .in0(multiplexer_2_out), .in1(multiplexer_6_out), .in2(out_27), .in3(adder_2_out), .out(out_29),
    .sel(S3_S4));  // open: en
  Multiplexer #(.select(2)) multiplexer_23 (
    .in0(multiplexer_3_out), .in1(multiplexer_7_out), .in2(out_30), .in3(adder_3_out), .out(out_31),
    .sel(S3_S4));  // open: en
  Multiplexer #(.select(2)) multiplexer_24 (
    .in0(multiplexer_4_out), .in1(multiplexer_8_out), .in2(out_33), .in3(adder_4_out), .out(out_32),
    .sel(S3_S4));  // open: en
endmodule
